// Logisim project molor_basic_processor.circ as structural Verilog: 4 circuits, main circuit cpu
module cpu (
  input  [31:0] INST,
  input  CLK,
  input  [31:0] DOUT,
  input  [31:0] INC,
  input  RESET,
  output [31:0] PC,
  output [31:0] MP,
  output [31:0] DIN,
  output [3:0] WE
);

  wire and_1_out, and_2_out, and_3_out, and_4_out, and_5_out, and_6_out, and_7_out, and_8_out,
       comparator_1_eq, comparator_1_gt, comparator_1_lt, comparator_2_eq, comparator_2_gt, comparator_2_lt,
       demultiplexer_1_out2, demultiplexer_1_out3, multiplexer_4_out, nand_1_out, nor_1_out, or_1_out,
       or_2_out, or_3_out, or_4_out;
  wire [31:0] adder_1_out, adder_2_out, bit_extender_1_out, bit_extender_2_out, multiplexer_1_out,
       multiplexer_2_out, multiplexer_3_out, multiplexer_5_out, multiplexer_6_out, register_memory_1_q1,
       register_memory_1_q2, register_memory_1_qd;

  Demultiplexer #(.select(2)) demultiplexer_1 (
    .out2(demultiplexer_1_out2), .out3(demultiplexer_1_out3), .in(1'b1), .sel(INST[1:0]));  // open: out0, out1
  and and_1 (and_1_out, demultiplexer_1_out2, or_3_out);
  nand nand_1 (nand_1_out, demultiplexer_1_out3, INST[31]);
  Multiplexer #(.width(32)) multiplexer_1 (
    .in0(register_memory_1_qd), .in1(multiplexer_3_out), .out(multiplexer_1_out), .sel(INST[5]));
  Multiplexer #(.width(32)) multiplexer_2 (
    .in0(adder_2_out), .in1(bit_extender_2_out), .out(multiplexer_2_out), .sel(INST[5]));
  and and_2 (and_2_out, INST[2], comparator_1_gt);
  Comparator #(.mode("unsigned"), .width(32)) comparator_1 (
    .a(register_memory_1_q1), .b(multiplexer_1_out), .gt(comparator_1_gt), .eq(comparator_1_eq),
    .lt(comparator_1_lt));
  and and_3 (and_3_out, INST[2], comparator_2_gt);
  Comparator #(.width(32)) comparator_2 (
    .a(register_memory_1_q1), .b(multiplexer_1_out), .gt(comparator_2_gt), .eq(comparator_2_eq),
    .lt(comparator_2_lt));
  assign bit_extender_1_out = {{16{INST[23]}}, INST[23:8]};  // Bit_Extender bit_extender_1
  and and_4 (and_4_out, INST[3], comparator_1_eq);
  and and_5 (and_5_out, INST[3], comparator_2_eq);
  Multiplexer #(.width(32)) multiplexer_3 (
    .in0(register_memory_1_q2), .in1(bit_extender_1_out), .out(multiplexer_3_out), .sel(INST[6]));
  nor nor_1 (nor_1_out, INST[2], INST[3], INST[4]);
  or or_1 (or_1_out, and_2_out, and_4_out, and_6_out);
  and and_6 (and_6_out, INST[4], comparator_1_lt);
  or or_2 (or_2_out, and_3_out, and_5_out, and_7_out);
  and and_7 (and_7_out, INST[4], comparator_2_lt);
  or or_3 (or_3_out, nor_1_out, INST[5]);
  Multiplexer multiplexer_4 (.in0(or_1_out), .in1(or_2_out), .out(multiplexer_4_out), .sel(INST[7]));
  Multiplexer #(.width(32)) multiplexer_5 (
    .in0(PC), .in1(register_memory_1_q1), .out(multiplexer_5_out), .sel(INST[6]));
  register_memory register_memory_1 (
    .RS1(INST[27:24]), .RS2(INST[23:20]), .RD(INST[31:28]), .DATA(multiplexer_2_out), .WE(and_1_out),
    .CLK(CLK), .RST(RESET), .Q1(register_memory_1_q1), .Q2(register_memory_1_q2), .QD(register_memory_1_qd));
  Adder #(.width(32)) adder_1 (.a(multiplexer_5_out), .b(bit_extender_1_out), .out(adder_1_out));  // open: cin, cout
  assign bit_extender_2_out = {{31{1'b0}}, multiplexer_4_out};  // Bit_Extender bit_extender_2
  or or_4 (or_4_out, nor_1_out, multiplexer_4_out);
  and and_8 (and_8_out, demultiplexer_1_out2, ~INST[5], or_4_out);  // AND_Gate
  Register #(.width(32)) PROG_CTR (.D(multiplexer_6_out), .en(nand_1_out), .clk(CLK), .Q(PC), .clr(RESET));
  Multiplexer #(.width(32)) multiplexer_6 (
    .in0(adder_2_out), .in1(adder_1_out), .out(multiplexer_6_out), .sel(and_8_out));
  Adder #(.width(32)) adder_2 (.a(PC), .b(INC), .out(adder_2_out));  // open: cin, cout
endmodule

module register_memory (
  input  [3:0] RS1,
  input  [3:0] RS2,
  input  [3:0] RD,
  input  [31:0] DATA,
  input  WE,
  input  CLK,
  input  RST,
  output [31:0] Q1,
  output [31:0] Q2,
  output [31:0] QD
);

  wire demultiplexer_1_out0, demultiplexer_1_out1, demultiplexer_1_out2, demultiplexer_1_out3,
       demultiplexer_1_out4, demultiplexer_1_out5, demultiplexer_1_out6, demultiplexer_1_out7,
       demultiplexer_1_out8, demultiplexer_1_out9, demultiplexer_1_out10, demultiplexer_1_out11,
       demultiplexer_1_out12, demultiplexer_1_out13, demultiplexer_1_out14;
  wire [31:0] register_1_q, register_2_q, register_3_q, register_4_q, register_5_q, register_6_q,
       register_7_q, register_8_q, register_9_q, register_10_q, register_11_q, register_12_q, register_13_q,
       register_14_q, register_15_q;

  Demultiplexer #(.select(4)) demultiplexer_1 (
    .out0(demultiplexer_1_out0), .out1(demultiplexer_1_out1), .out2(demultiplexer_1_out2),
    .out3(demultiplexer_1_out3), .out4(demultiplexer_1_out4), .out5(demultiplexer_1_out5),
    .out6(demultiplexer_1_out6), .out7(demultiplexer_1_out7), .out8(demultiplexer_1_out8),
    .out9(demultiplexer_1_out9), .out10(demultiplexer_1_out10), .out11(demultiplexer_1_out11),
    .out12(demultiplexer_1_out12), .out13(demultiplexer_1_out13), .out14(demultiplexer_1_out14), .in(CLK),
    .sel(RD));  // open: out15
  Register #(.width(32)) register_1 (.D(DATA), .en(WE), .clk(demultiplexer_1_out0), .Q(register_1_q), .clr(RST));
  Register #(.width(32)) register_2 (.D(DATA), .en(WE), .clk(demultiplexer_1_out1), .Q(register_2_q), .clr(RST));
  Register #(.width(32)) register_3 (.D(DATA), .en(WE), .clk(demultiplexer_1_out2), .Q(register_3_q), .clr(RST));
  Register #(.width(32)) register_4 (.D(DATA), .en(WE), .clk(demultiplexer_1_out3), .Q(register_4_q), .clr(RST));
  Register #(.width(32)) register_5 (.D(DATA), .en(WE), .clk(demultiplexer_1_out4), .Q(register_5_q), .clr(RST));
  Register #(.width(32)) register_6 (.D(DATA), .en(WE), .clk(demultiplexer_1_out5), .Q(register_6_q), .clr(RST));
  Register #(.width(32)) register_7 (.D(DATA), .en(WE), .clk(demultiplexer_1_out6), .Q(register_7_q), .clr(RST));
  Register #(.width(32)) register_8 (.D(DATA), .en(WE), .clk(demultiplexer_1_out7), .Q(register_8_q), .clr(RST));
  Register #(.width(32)) register_9 (.D(DATA), .en(WE), .clk(demultiplexer_1_out8), .Q(register_9_q), .clr(RST));
  Register #(.width(32)) register_10 (.D(DATA), .en(WE), .clk(demultiplexer_1_out9), .Q(register_10_q), .clr(RST));
  Register #(.width(32)) register_11 (.D(DATA), .en(WE), .clk(demultiplexer_1_out10), .Q(register_11_q), .clr(RST));
  Register #(.width(32)) register_12 (.D(DATA), .en(WE), .clk(demultiplexer_1_out11), .Q(register_12_q), .clr(RST));
  Register #(.width(32)) register_13 (.D(DATA), .en(WE), .clk(demultiplexer_1_out12), .Q(register_13_q), .clr(RST));
  Register #(.width(32)) register_14 (.D(DATA), .en(WE), .clk(demultiplexer_1_out13), .Q(register_14_q), .clr(RST));
  Register #(.width(32)) register_15 (.D(DATA), .en(WE), .clk(demultiplexer_1_out14), .Q(register_15_q), .clr(RST));
  Multiplexer #(.select(4), .width(32)) multiplexer_1 (
    .in0(register_1_q), .in1(register_2_q), .in2(register_3_q), .in3(register_4_q), .in4(register_5_q),
    .in5(register_6_q), .in6(register_7_q), .in7(register_8_q), .in8(register_9_q), .in9(register_10_q),
    .in10(register_11_q), .in11(register_12_q), .in12(register_13_q), .in13(register_14_q),
    .in14(register_15_q), .in15({32{1'b0}}), .out(Q1), .sel(RS1));
  Multiplexer #(.select(4), .width(32)) multiplexer_2 (
    .in0(register_1_q), .in1(register_2_q), .in2(register_3_q), .in3(register_4_q), .in4(register_5_q),
    .in5(register_6_q), .in6(register_7_q), .in7(register_8_q), .in8(register_9_q), .in9(register_10_q),
    .in10(register_11_q), .in11(register_12_q), .in12(register_13_q), .in13(register_14_q),
    .in14(register_15_q), .in15({32{1'b0}}), .out(Q2), .sel(RS2));
  Multiplexer #(.select(4), .width(32)) multiplexer_3 (
    .in0(register_1_q), .in1(register_2_q), .in2(register_3_q), .in3(register_4_q), .in4(register_5_q),
    .in5(register_6_q), .in6(register_7_q), .in7(register_8_q), .in8(register_9_q), .in9(register_10_q),
    .in10(register_11_q), .in11(register_12_q), .in12(register_13_q), .in13(register_14_q),
    .in14(register_15_q), .in15({32{1'b0}}), .out(QD), .sel(RD));
endmodule

module main (
  input  in_1
);

  wire clock_1_out;
  wire [3:0] cpu_1_we;
  wire [7:0] rom_1_p2, rom_1_p3, rom_1_p4, rom_1_p5;
  wire [15:0] bit_extender_1_out, bit_extender_2_out;
  wire [31:0] cpu_1_din, cpu_1_mp, cpu_1_pc, memory64kx8_1_dout;

  Clock clock_1 (.out(clock_1_out));
  Bit_Extender #(.in_width(32)) bit_extender_1 (.in(cpu_1_pc), .out(bit_extender_1_out));
  // ROM #(.addrWidth(16), .line("quad")) rom_1: pin names not known; wires that end beside it: bit_extender_1_out, rom_1_p2, rom_1_p3, rom_1_p4, rom_1_p5
  memory64kx8 memory64kx8_1 (
    .ADDR(bit_extender_2_out), .WE(cpu_1_we), .CLK(clock_1_out), .DIN(cpu_1_din), .DOUT(memory64kx8_1_dout));
  cpu cpu_1 (
    .INST({rom_1_p5, rom_1_p4, rom_1_p3, rom_1_p2}), .CLK(clock_1_out), .DOUT(memory64kx8_1_dout),
    .INC(32'h4), .RESET(in_1), .PC(cpu_1_pc), .MP(cpu_1_mp), .DIN(cpu_1_din), .WE(cpu_1_we));
  Bit_Extender #(.in_width(32), .\type ("zero")) bit_extender_2 (.in(cpu_1_mp), .out(bit_extender_2_out));

  // Notes on the sheet:
  //   contents of rom_1 (hex, n*v repeats v):
  //   3 0 0 0 3 0 0 0 2 20 0 df 3 0 0 0 5e 0 0 ff 3 0 0 0 3 0 0 0 3 0 0 0 3 0 0 0 3 0 0 0 3 0 0 0 3 0 0 0
  //   3 0 0 0 5e 0 0 fd
endmodule

module memory64kx8 (
  input  [15:0] ADDR,
  input  [3:0] WE,
  input  CLK,
  input  [31:0] DIN,
  output [31:0] DOUT
);

  wire comparator_1_lt, comparator_2_lt, comparator_3_lt, not_1_out, not_2_out, not_3_out;
  wire [7:0] multiplexer_1_out, multiplexer_2_out, multiplexer_3_out, multiplexer_4_out, ram_1_dout,
       ram_2_dout, ram_3_dout, ram_4_dout;
  wire [13:0] adder_1_out, adder_2_out, adder_3_out;

  Multiplexer #(.select(2), .width(8)) multiplexer_1 (
    .in0(DIN[7:0]), .in1(DIN[31:24]), .in2(DIN[23:16]), .in3(DIN[15:8]), .out(multiplexer_1_out),
    .sel(ADDR[1:0]));
  Multiplexer #(.select(2), .width(8)) multiplexer_2 (
    .in0(DIN[15:8]), .in1(DIN[7:0]), .in2(DIN[31:24]), .in3(DIN[23:16]), .out(multiplexer_2_out),
    .sel(ADDR[1:0]));
  Multiplexer #(.select(2), .width(8)) multiplexer_3 (
    .in0(DIN[23:16]), .in1(DIN[15:8]), .in2(DIN[7:0]), .in3(DIN[31:24]), .out(multiplexer_3_out),
    .sel(ADDR[1:0]));
  Multiplexer #(.select(2), .width(8)) multiplexer_4 (
    .in0(DIN[31:24]), .in1(DIN[23:16]), .in2(DIN[15:8]), .in3(DIN[7:0]), .out(multiplexer_4_out),
    .sel(ADDR[1:0]));
  Comparator #(.mode("unsigned"), .width(2)) comparator_1 (
    .a(ADDR[1:0]), .b(2'b01), .lt(comparator_1_lt));  // open: gt, eq
  not not_1 (not_1_out, comparator_1_lt);
  Comparator #(.mode("unsigned"), .width(2)) comparator_2 (
    .a(ADDR[1:0]), .b(2'b10), .lt(comparator_2_lt));  // open: gt, eq
  not not_2 (not_2_out, comparator_2_lt);
  Comparator #(.mode("unsigned"), .width(2)) comparator_3 (
    .a(ADDR[1:0]), .b(2'b11), .lt(comparator_3_lt));  // open: gt, eq
  not not_3 (not_3_out, comparator_3_lt);
  Adder #(.width(14)) adder_1 (.a(ADDR[15:2]), .b({14{1'b0}}), .out(adder_1_out), .cin(not_2_out));  // open: cout
  RAM #(.addrWidth(14), .enables("line")) ram_1 (
    .addr(adder_2_out), .we(WE[0]), .clk(CLK), .din(multiplexer_1_out), .dout(ram_1_dout));
  Adder #(.width(14)) adder_2 (.a(ADDR[15:2]), .b({14{1'b0}}), .out(adder_2_out), .cin(not_1_out));  // open: cout
  RAM #(.addrWidth(14), .enables("line")) ram_2 (
    .addr(adder_1_out), .we(WE[1]), .clk(CLK), .din(multiplexer_2_out), .dout(ram_2_dout));
  RAM #(.addrWidth(14), .enables("line")) ram_3 (
    .addr(adder_3_out), .we(WE[2]), .clk(CLK), .din(multiplexer_3_out), .dout(ram_3_dout));
  Adder #(.width(14)) adder_3 (.a(ADDR[15:2]), .b({14{1'b0}}), .out(adder_3_out), .cin(not_3_out));  // open: cout
  RAM #(.addrWidth(14), .enables("line")) ram_4 (
    .addr(ADDR[15:2]), .we(WE[3]), .clk(CLK), .din(multiplexer_4_out), .dout(ram_4_dout));
  Multiplexer #(.select(2), .width(8)) multiplexer_5 (
    .in0(ram_1_dout), .in1(ram_2_dout), .in2(ram_3_dout), .in3(ram_4_dout), .out(DOUT[7:0]), .sel(ADDR[1:0]));
  Multiplexer #(.select(2), .width(8)) multiplexer_6 (
    .in0(ram_2_dout), .in1(ram_3_dout), .in2(ram_4_dout), .in3(ram_1_dout), .out(DOUT[15:8]), .sel(ADDR[1:0]));
  Multiplexer #(.select(2), .width(8)) multiplexer_7 (
    .in0(ram_3_dout), .in1(ram_4_dout), .in2(ram_1_dout), .in3(ram_2_dout), .out(DOUT[23:16]), .sel(ADDR[1:0]));
  Multiplexer #(.select(2), .width(8)) multiplexer_8 (
    .in0(ram_4_dout), .in1(ram_1_dout), .in2(ram_2_dout), .in3(ram_3_dout), .out(DOUT[31:24]), .sel(ADDR[1:0]));
endmodule
